# Fritzing sketch LaserGuidanceSystem (saved by Fritzing 0.9.10b)
breadboards: 1

parts:
  Mod1 = seeeduino-xiao
  U1 = LM124-324 Quad Opamp [package="DIP (Dual Inline)"]
  R1 = Resistor [tolerance=±5% power=0.25 resistance=100k package=THT]
  C1 = Ceramic Capacitor [capacitance=0.1nF voltage=35V package="100 mil [THT, multilayer]"]
  C2 = Ceramic Capacitor [capacitance=10µF voltage=35V package="100 mil [THT, multilayer]"]
  R3 = Resistor [tolerance=±5% power=0.25 resistance=100k package=THT]
  C5 = Ceramic Capacitor [capacitance=0.1nF voltage=35V package="100 mil [THT, multilayer]"]
  C6 = Ceramic Capacitor [capacitance=10µF voltage=35V package="100 mil [THT, multilayer]"]
  C7 = Ceramic Capacitor [capacitance=0.1nF voltage=35V package="100 mil [THT, multilayer]"]
  C8 = Ceramic Capacitor [capacitance=10µF voltage=35V package="100 mil [THT, multilayer]"]
  R4 = Resistor [tolerance=±5% power=0.25 resistance=100k package=THT]
  C9 = Ceramic Capacitor [capacitance=0.1nF voltage=35V package="100 mil [THT, multilayer]"]
  C10 = Ceramic Capacitor [capacitance=10µF voltage=35V package="100 mil [THT, multilayer]"]
  R5 = Resistor [tolerance=±5% power=0.25 resistance=100k package=THT]
  P1 = S1133 Si Photodiode [package="8mm Ceramic [THT]"]
  P2 = S1133 Si Photodiode [package="8mm Ceramic [THT]"]
  P3 = S1133 Si Photodiode [package="8mm Ceramic [THT]"]
  P4 = S1133 Si Photodiode [package="8mm Ceramic [THT]"]

nets:
  N1: Mod1.D0, U1.1OUT
  N2: Mod1.D1, U1.2OUT
  N3: Mod1.D2, U1.4OUT
  N4: Mod1.D3, U1.3OUT
  N5: Mod1.GND, U1.1IN+, U1.2IN+, U1.3IN+, U1.VCC-, U1.4IN+, C2.1, C6.1, C8.1, P1.anode, P2.anode, P3.anode, P4.anode
  N6: Mod1.5V, U1.VCC+
  N7: U1.1IN-, R1.Pin_0, C1.0
  N8: U1.2IN-, R3.Pin_0, C5.0
  N9: U1.3IN-, C9.0, R5.Pin_0
  N10: U1.4IN-, C7.0, R4.Pin_0
  N11: R1.Pin_1, C1.1, C2.0, P1.cathode
  N12: R3.Pin_1, C5.1, C6.0, P2.cathode
  N13: C7.1, C8.0, R4.Pin_1, P4.cathode
  N14: C9.1, C10.0, R5.Pin_1, P3.cathode

custom parts:
  seeeduino-xiao: Seeeduino XIAO processor board.
